// Logisim project flip_flop_d.circ as structural Verilog: 1 circuit, main circuit main
module main (
  input  in_1,
  input  in_2,
  output out_3,
  output out_4,
  output out_5
);

  wire nand_1_out, nand_2_out, not_1_out, not_2_out, not_3_out;

  not not_1 (not_1_out, in_2);
  not not_2 (not_2_out, not_1_out);
  and and_1 (out_4, in_2, not_3_out);
  not not_3 (not_3_out, not_2_out);
  nand nand_1 (nand_1_out, in_1, out_4);
  nand nand_2 (nand_2_out, nand_1_out, out_4);
  nand nand_3 (out_3, nand_1_out, out_5);
  nand nand_4 (out_5, out_3, nand_2_out);
endmodule
