// Logisim project flip_flop_jk.circ as structural Verilog: 1 circuit, main circuit main
module main (
  input  in_1,
  input  in_2,
  input  in_3,
  output out_4,
  output out_5,
  output out_6
);

  wire not_1_out, not_2_out, not_3_out;

  not not_1 (not_1_out, in_2);
  not not_2 (not_2_out, not_1_out);
  not not_3 (not_3_out, not_2_out);
  and and_1 (out_4, in_2, not_3_out);
  J_K_Flip_Flop j_k_ff_1 (.J(in_1), .K(out_4), .clk(in_3), .Q(out_5), .Qn(out_6));  // open: preset, reset
endmodule
