// Logisim project flip_flop_rs.circ as structural Verilog: 1 circuit, main circuit main
module main (
  input  R,
  input  in_2,
  input  S,
  output Q,
  output out_5,
  output Q0
);

  wire nand_1_out, nand_2_out, not_1_out, not_2_out, not_3_out;

  not not_1 (not_1_out, in_2);
  not not_2 (not_2_out, not_1_out);
  not not_3 (not_3_out, not_2_out);
  and and_1 (out_5, in_2, not_3_out);
  nand nand_1 (nand_1_out, R, out_5);
  nand nand_2 (nand_2_out, out_5, S);
  nand nand_3 (Q, nand_1_out, Q0);
  nand nand_4 (Q0, Q, nand_2_out);
endmodule
