// Logisim project lauch_rs.circ as structural Verilog: 1 circuit, main circuit main
module main (
  input  R,
  input  in_2,
  input  S,
  output Q,
  output Q0
);

  wire nand_1_out, nand_2_out;

  nand nand_1 (nand_1_out, R, in_2);
  nand nand_2 (nand_2_out, in_2, S);
  nand nand_3 (Q, nand_1_out, Q0);
  nand nand_4 (Q0, Q, nand_2_out);
endmodule
